// Logisim project control-logic.circ as structural Verilog: 1 circuit, main circuit control_logic
module control_logic (
  input  [31:0] Instruction,
  input  BrEq,
  input  BrLt,
  output PCSel,
  output RegWEn,
  output [2:0] ImmSel,
  output BrUn,
  output ASel,
  output BSel,
  output [3:0] ALUSel,
  output MemWEn,
  output [1:0] WBSel
);

  wire add, add_mul_sub, addi, and_10_out, and_11_out, and_12_out, and_13_out, and_14_out, and_15_out,
       and_16_out, and_17_out, and_r, andi, B_Type, beq, bge, bgeu, blt, bltu, bne, comparator_5_eq,
       comparator_5_lt, comparator_6_eq, comparator_7_eq, comparator_8_eq, comparator_9_eq, comparator_10_eq,
       comparator_11_eq, comparator_12_eq, comparator_13_eq, comparator_14_eq, comparator_15_eq,
       comparator_15_lt, comparator_16_eq, comparator_17_eq, comparator_17_lt, comparator_18_eq,
       comparator_19_eq, comparator_20_eq, comparator_21_eq, comparator_22_eq, comparator_22_gt,
       comparator_23_eq, comparator_24_eq, comparator_25_eq, comparator_26_eq, comparator_27_eq,
       comparator_28_eq, comparator_29_eq, comparator_30_eq, I_Type, mul, mulh, mulhu, multiplexer_1_out,
       not_1_out, not_2_out, not_3_out, or_1_out, or_2_out, or_r, ori, R_Type, S_Type, sll_mulh, sll_r, slli,
       slt, slti, sr_i, sra_r, srai, srl_r, srl_sra, srli, sub, xor_r, xori;
  wire [5:0] priority_encoder_1_out;
  wire [15:14] rom_1_data;

  Comparator #(.width(7)) comparator_1 (.a(Instruction[6:0]), .b(7'b0010011), .eq(I_Type));  // open: gt, lt
  Comparator #(.width(7)) comparator_2 (.a(Instruction[6:0]), .b(7'b0110011), .eq(R_Type));  // open: gt, lt
  Comparator #(.width(7)) comparator_3 (.a(Instruction[6:0]), .b(7'b1100011), .eq(B_Type));  // open: gt, lt
  Comparator #(.width(7)) comparator_4 (.a(Instruction[6:0]), .b(7'b0100011), .eq(S_Type));  // open: gt, lt
  ROM #(.addrWidth(6), .dataWidth(16)) rom_1 (
    .addr(priority_encoder_1_out),
    .data({rom_1_data, WBSel, MemWEn, ALUSel, BSel, ASel, BrUn, ImmSel, RegWEn}));
  Priority_Encoder #(.select_enc(6)) priority_encoder_1 (
    .in0(add), .in1(mul), .in2(sub), .in3(sll_r), .in4(mulh), .in5(mulhu), .in6(slt), .in7(xor_r),
    .in8(srl_r), .in9(sra_r), .in10(or_r), .in11(and_r), .in15(addi), .in16(slli), .in17(slti), .in18(xori),
    .in19(srli), .in20(srai), .in21(ori), .in22(andi), .in26(beq), .in27(bne), .in28(blt), .in29(bge),
    .in30(bltu), .in31(bgeu), .out(priority_encoder_1_out));  // open: in12, in13, in14, in23, in24, in25, in32, in33, in34, in35, in36, in37, in38, in39, in40, in41, in42, in43, in44, in45, in46, in47, in48, in49, in50, in51, in52, in53, in54, in55, in56, in57, in58, in59, in60, in61, in62, in63, gs, en_out, en_in
  Comparator #(.width(7)) comparator_5 (
    .a(Instruction[31:25]), .b(7'b0100000), .eq(comparator_5_eq), .lt(comparator_5_lt));  // open: gt
  Comparator #(.width(3)) comparator_6 (.a(Instruction[14:12]), .b(3'b000), .eq(comparator_6_eq));  // open: gt, lt
  Comparator #(.width(3)) comparator_7 (.a(Instruction[14:12]), .b(3'b001), .eq(comparator_7_eq));  // open: gt, lt
  Comparator #(.width(3)) comparator_8 (.a(Instruction[14:12]), .b(3'b010), .eq(comparator_8_eq));  // open: gt, lt
  Comparator #(.width(3)) comparator_9 (.a(Instruction[14:12]), .b(3'b100), .eq(comparator_9_eq));  // open: gt, lt
  Comparator #(.width(3)) comparator_10 (.a(Instruction[14:12]), .b(3'b101), .eq(comparator_10_eq));  // open: gt, lt
  Comparator #(.width(3)) comparator_11 (.a(Instruction[14:12]), .b(3'b110), .eq(comparator_11_eq));  // open: gt, lt
  Comparator #(.width(3)) comparator_12 (.a(Instruction[14:12]), .b(3'b111), .eq(comparator_12_eq));  // open: gt, lt
  and and_1 (addi, I_Type, comparator_6_eq);
  and and_2 (slli, I_Type, comparator_7_eq);
  and and_3 (slti, I_Type, comparator_8_eq);
  and and_4 (xori, I_Type, comparator_9_eq);
  and and_5 (sr_i, I_Type, comparator_10_eq);
  and and_6 (srai, sr_i, comparator_5_eq);
  and and_7 (srli, comparator_5_lt, sr_i);
  and and_8 (ori, I_Type, comparator_11_eq);
  and and_9 (andi, I_Type, comparator_12_eq);
  not not_1 (not_1_out, BrEq);
  not not_2 (not_2_out, BrLt);
  not not_3 (not_3_out, BrLt);
  and and_10 (and_10_out, BrEq, beq);
  and and_11 (and_11_out, not_1_out, bne);
  and and_12 (and_12_out, BrLt, blt);
  and and_13 (and_13_out, not_2_out, bge);
  and and_14 (and_14_out, BrEq, bge);
  and and_15 (and_15_out, BrLt, bltu);
  and and_16 (and_16_out, not_3_out, bgeu);
  and and_17 (and_17_out, BrEq, bgeu);
  or or_1 (or_1_out, and_13_out, and_14_out);
  or or_2 (or_2_out, and_16_out, and_17_out);
  Comparator #(.width(3)) comparator_13 (.a(Instruction[14:12]), .b(3'b000), .eq(comparator_13_eq));  // open: gt, lt
  Comparator #(.width(7)) comparator_14 (
    .a(Instruction[31:25]), .b(7'b0100000), .eq(comparator_14_eq));  // open: gt, lt
  Comparator #(.width(7)) comparator_15 (
    .a(Instruction[31:25]), .b(7'b0000001), .eq(comparator_15_eq), .lt(comparator_15_lt));  // open: gt
  Comparator #(.width(3)) comparator_16 (.a(Instruction[14:12]), .b(3'b001), .eq(comparator_16_eq));  // open: gt, lt
  Comparator #(.width(7)) comparator_17 (
    .a(Instruction[31:25]), .b(7'b0000001), .eq(comparator_17_eq), .lt(comparator_17_lt));  // open: gt
  Comparator #(.width(3)) comparator_18 (.a(Instruction[14:12]), .b(3'b011), .eq(comparator_18_eq));  // open: gt, lt
  Comparator #(.width(3)) comparator_19 (.a(Instruction[14:12]), .b(3'b010), .eq(comparator_19_eq));  // open: gt, lt
  Comparator #(.width(3)) comparator_20 (.a(Instruction[14:12]), .b(3'b100), .eq(comparator_20_eq));  // open: gt, lt
  Comparator #(.width(3)) comparator_21 (.a(Instruction[14:12]), .b(3'b101), .eq(comparator_21_eq));  // open: gt, lt
  Comparator #(.width(7)) comparator_22 (
    .a(Instruction[31:25]), .b({7{1'b0}}), .gt(comparator_22_gt), .eq(comparator_22_eq));  // open: lt
  Comparator #(.width(3)) comparator_23 (.a(Instruction[14:12]), .b(3'b110), .eq(comparator_23_eq));  // open: gt, lt
  Comparator #(.width(3)) comparator_24 (.a(Instruction[14:12]), .b(3'b111), .eq(comparator_24_eq));  // open: gt, lt
  and and_18 (add_mul_sub, R_Type, comparator_13_eq);
  and and_19 (sll_mulh, R_Type, comparator_16_eq);
  and and_20 (mulhu, R_Type, comparator_18_eq);
  and and_21 (slt, R_Type, comparator_19_eq);
  and and_22 (xor_r, R_Type, comparator_20_eq);
  and and_23 (srl_sra, R_Type, comparator_21_eq);
  and and_24 (or_r, R_Type, comparator_23_eq);
  and and_25 (and_r, R_Type, comparator_24_eq);
  and and_26 (sub, add_mul_sub, comparator_14_eq);
  and and_27 (mul, add_mul_sub, comparator_15_eq);
  and and_28 (add, comparator_15_lt, add_mul_sub);
  and and_29 (mulh, sll_mulh, comparator_17_eq);
  and and_30 (sll_r, comparator_17_lt, sll_mulh);
  and and_31 (sra_r, srl_sra, comparator_22_eq);
  and and_32 (srl_r, comparator_22_gt, srl_sra);
  Multiplexer #(.select(3)) multiplexer_1 (
    .in0(and_10_out), .in1(and_11_out), .in4(and_12_out), .in5(or_1_out), .in6(and_15_out), .in7(or_2_out),
    .out(multiplexer_1_out), .sel(Instruction[14:12]));  // open: in2, in3
  and and_33 (PCSel, B_Type, multiplexer_1_out);
  Comparator #(.width(3)) comparator_25 (.a(Instruction[14:12]), .b(3'b000), .eq(comparator_25_eq));  // open: gt, lt
  Comparator #(.width(3)) comparator_26 (.a(Instruction[14:12]), .b(3'b001), .eq(comparator_26_eq));  // open: gt, lt
  Comparator #(.width(3)) comparator_27 (.a(Instruction[14:12]), .b(3'b100), .eq(comparator_27_eq));  // open: gt, lt
  Comparator #(.width(3)) comparator_28 (.a(Instruction[14:12]), .b(3'b101), .eq(comparator_28_eq));  // open: gt, lt
  Comparator #(.width(3)) comparator_29 (.a(Instruction[14:12]), .b(3'b110), .eq(comparator_29_eq));  // open: gt, lt
  Comparator #(.width(3)) comparator_30 (.a(Instruction[14:12]), .b(3'b111), .eq(comparator_30_eq));  // open: gt, lt
  and and_34 (beq, B_Type, comparator_25_eq);
  and and_35 (bne, B_Type, comparator_26_eq);
  and and_36 (blt, B_Type, comparator_27_eq);
  and and_37 (bge, B_Type, comparator_28_eq);
  and and_38 (bltu, B_Type, comparator_29_eq);
  and and_39 (bgeu, B_Type, comparator_30_eq);

  // Other names for the same wires on the sheet: Opcode[6:0] = Instruction[6:0]; Funct3[2:0] = Instruction[14:12];
  //   Funct7[6:0] = Instruction[31:25]

  // Notes on the sheet:
  //   INPUTS to your circuit
  //   Connect ROM Input here ->
  //   contents of rom_1 (hex, n*v repeats v):
  //   1001 1401 1601 1081 1481 1581 1101 1201 1281 1681 1301 1381 0 0 0 1041 10c1 1141 1241 12c1 16c1 1341
  //   13c1 0 0 0 4*1064 1074 1074
  //   ROM FOR CONTROL LOGIC
  //   DON'T CHANGE THE LOCATIONS OF THE INPUTS AND OUTPUTS!
  //   This is only if you choose to do the ROM option
  //   CONNECT
  //   WIRE
  //   TO
  //   USE
  //   ROM
  //   OUTPUT from your circuit
  //   Reminder: If using ROM, use combinational logic for PCSel
endmodule
