// Logisim project regfile.circ as structural Verilog: 1 circuit, main circuit regfile
module regfile (
  input  [4:0] ReadIndex1,
  input  [4:0] ReadIndex2,
  input  [4:0] WriteIndex,
  input  [31:0] WriteData,
  input  RegWEn,
  input  clk,
  output [31:0] ra,
  output [31:0] sp,
  output [31:0] t0,
  output [31:0] t1,
  output [31:0] t2,
  output [31:0] s0,
  output [31:0] s1,
  output [31:0] a0,
  output [31:0] ReadData1,
  output [31:0] ReadData2
);

  wire [31:0] x0, x0WD, x1WD, x2WD, x3WD, x4WD, x5WD, x6WD, x7WD, x8WD, x9, x9WD, x10, x10WD, x11, x11WD,
       x12, x12WD, x13, x13WD, x14, x14WD, x15, x15WD, x16, x16WD, x17, x17WD, x18, x18WD, x19, x19WD, x20,
       x20WD, x21, x21WD, x22, x22WD, x23, x23WD, x24, x24WD, x25, x25WD, x26, x26WD, x27, x27WD, x28, x28WD,
       x29, x29WD, x30, x30WD, x31, x31WD;

  Demultiplexer #(.select(5), .width(32)) demultiplexer_1 (
    .out0(x0WD), .out1(x1WD), .out2(x2WD), .out3(x3WD), .out4(x4WD), .out5(x5WD), .out6(x6WD), .out7(x7WD),
    .out8(x8WD), .out9(x9WD), .out10(x10WD), .out11(x11WD), .out12(x12WD), .out13(x13WD), .out14(x14WD),
    .out15(x15WD), .out16(x16WD), .out17(x17WD), .out18(x18WD), .out19(x19WD), .out20(x20WD), .out21(x21WD),
    .out22(x22WD), .out23(x23WD), .out24(x24WD), .out25(x25WD), .out26(x26WD), .out27(x27WD), .out28(x28WD),
    .out29(x29WD), .out30(x30WD), .out31(x31WD), .in(WriteData), .sel(WriteIndex));
  Multiplexer #(.select(5), .width(32)) multiplexer_1 (
    .in0(x0), .in1(ra), .in2(sp), .in3(t0), .in4(t1), .in5(t2), .in6(s0), .in7(s1), .in8(a0), .in9(x9),
    .in10(x10), .in11(x11), .in12(x12), .in13(x13), .in14(x14), .in15(x15), .in16(x16), .in17(x17),
    .in18(x18), .in19(x19), .in20(x20), .in21(x21), .in22(x22), .in23(x23), .in24(x24), .in25(x25),
    .in26(x26), .in27(x27), .in28(x28), .in29(x29), .in30(x30), .in31(x31), .out(ReadData1), .sel(ReadIndex1));
  Multiplexer #(.select(5), .width(32)) multiplexer_2 (
    .in0(x0), .in1(ra), .in2(sp), .in3(t0), .in4(t1), .in5(t2), .in6(s0), .in7(s1), .in8(a0), .in9(x9),
    .in10(x10), .in11(x11), .in12(x12), .in13(x13), .in14(x14), .in15(x15), .in16(x16), .in17(x17),
    .in18(x18), .in19(x19), .in20(x20), .in21(x21), .in22(x22), .in23(x23), .in24(x24), .in25(x25),
    .in26(x26), .in27(x27), .in28(x28), .in29(x29), .in30(x30), .in31(x31), .out(ReadData2), .sel(ReadIndex2));
  Register #(.width(32)) u_x0 (.D(x0WD), .en(RegWEn), .clk(clk), .Q(x0), .clr(1'b1));
  Register #(.width(32)) x1 (.D(x1WD), .en(RegWEn), .clk(clk), .Q(ra));  // open: clr
  Register #(.width(32)) x2 (.D(x2WD), .en(RegWEn), .clk(clk), .Q(sp));  // open: clr
  Register #(.width(32)) x3 (.D(x3WD), .en(RegWEn), .clk(clk), .Q(t0));  // open: clr
  Register #(.width(32)) x4 (.D(x4WD), .en(RegWEn), .clk(clk), .Q(t1));  // open: clr
  Register #(.width(32)) register_1 (.D(x5WD), .en(RegWEn), .clk(clk), .Q(t2));  // open: clr
  Register #(.width(32)) register_2 (.D(x6WD), .en(RegWEn), .clk(clk), .Q(s0));  // open: clr
  Register #(.width(32)) register_3 (.D(x7WD), .en(RegWEn), .clk(clk), .Q(s1));  // open: clr
  Register #(.width(32)) register_4 (.D(x8WD), .en(RegWEn), .clk(clk), .Q(a0));  // open: clr
  Register #(.width(32)) register_5 (.D(x9WD), .en(RegWEn), .clk(clk), .Q(x9));  // open: clr
  Register #(.width(32)) register_6 (.D(x10WD), .en(RegWEn), .clk(clk), .Q(x10));  // open: clr
  Register #(.width(32)) register_7 (.D(x11WD), .en(RegWEn), .clk(clk), .Q(x11));  // open: clr
  Register #(.width(32)) register_8 (.D(x12WD), .en(RegWEn), .clk(clk), .Q(x12));  // open: clr
  Register #(.width(32)) register_9 (.D(x13WD), .en(RegWEn), .clk(clk), .Q(x13));  // open: clr
  Register #(.width(32)) register_10 (.D(x14WD), .en(RegWEn), .clk(clk), .Q(x14));  // open: clr
  Register #(.width(32)) register_11 (.D(x15WD), .en(RegWEn), .clk(clk), .Q(x15));  // open: clr
  Register #(.width(32)) register_12 (.D(x16WD), .en(RegWEn), .clk(clk), .Q(x16));  // open: clr
  Register #(.width(32)) register_13 (.D(x17WD), .en(RegWEn), .clk(clk), .Q(x17));  // open: clr
  Register #(.width(32)) register_14 (.D(x18WD), .en(RegWEn), .clk(clk), .Q(x18));  // open: clr
  Register #(.width(32)) register_15 (.D(x19WD), .en(RegWEn), .clk(clk), .Q(x19));  // open: clr
  Register #(.width(32)) register_16 (.D(x20WD), .en(RegWEn), .clk(clk), .Q(x20));  // open: clr
  Register #(.width(32)) register_17 (.D(x21WD), .en(RegWEn), .clk(clk), .Q(x21));  // open: clr
  Register #(.width(32)) register_18 (.D(x22WD), .en(RegWEn), .clk(clk), .Q(x22));  // open: clr
  Register #(.width(32)) register_19 (.D(x23WD), .en(RegWEn), .clk(clk), .Q(x23));  // open: clr
  Register #(.width(32)) register_20 (.D(x24WD), .en(RegWEn), .clk(clk), .Q(x24));  // open: clr
  Register #(.width(32)) register_21 (.D(x25WD), .en(RegWEn), .clk(clk), .Q(x25));  // open: clr
  Register #(.width(32)) register_22 (.D(x26WD), .en(RegWEn), .clk(clk), .Q(x26));  // open: clr
  Register #(.width(32)) register_23 (.D(x27WD), .en(RegWEn), .clk(clk), .Q(x27));  // open: clr
  Register #(.width(32)) register_24 (.D(x28WD), .en(RegWEn), .clk(clk), .Q(x28));  // open: clr
  Register #(.width(32)) register_25 (.D(x29WD), .en(RegWEn), .clk(clk), .Q(x29));  // open: clr
  Register #(.width(32)) register_26 (.D(x30WD), .en(RegWEn), .clk(clk), .Q(x30));  // open: clr
  Register #(.width(32)) register_27 (.D(x31WD), .en(RegWEn), .clk(clk), .Q(x31));  // open: clr

  // Notes on the sheet:
  //   INPUTS to your circuit
  //   DON'T CHANGE THE LOCATIONS OF THE INPUTS AND OUTPUTS!
  //   These are DEBUG/TEST outputs from your circuit.
  //   OUTPUTS from your circuit
endmodule
